# Fritzing sketch mq4-layout (saved by Fritzing 0.8.7b)
breadboards: 1

parts:
  Composant1 = Arduino Leonardo (Rev3b)
  Composant2 = Gas Sensor Breakout Board
  R1 = Resistor [tolerance=±5% resistance=10k package=THT]

nets:
  GND: Composant1.GND, Composant2.GND, R1.Pin_1
  N1: Composant1.A0, Composant2.B1, R1.Pin_0
  N2: Composant2.H1, Composant2.A1
