# Fritzing sketch sound_detector_layout (saved by Fritzing 0.8.7b)
breadboards: 1

parts:
  Composant1 = Arduino Leonardo (Rev3b)
  Composant2 = Breakout Board for Electret Microphone

nets:
  5V: Composant1.5V, Composant2.VCC
  GND: Composant1.GND, Composant2.GND
  N1: Composant1.A0, Composant2.AUD
